# Fritzing sketch BombDefuse (saved by Fritzing 0.9.3b)

parts:
  Composant1 = Arduino Mega 2560 (Rev3)
  Composant2 = RFID-RC522-v2
  OLED_I2C1 = OLED 128x64 I2C Monochrome Display
  Keypad4x1 = Keypad Membran 4x4
  S3 = Square Pushbutton
  R11 = Resistor [tolerance=±5% resistance=10k package=THT]
  KeyLock = Square Pushbutton
  R12 = Resistor [tolerance=±5% resistance=10k package=THT]
  J3 = Piezo Speaker
  LED3 = LED - 5mm [color="Red (633nm)" package="5 mm [THT]"]
  R13 = Resistor [tolerance=±5% resistance=220 package=THT]
  R14 = Resistor [tolerance=±5% resistance=220 package=THT]
  R15 = Rotary Potentiometer (Large) [maximum_resistance=100kΩ package=THT]
  LCD2004-I2C1 = LCD2004-I2C
  S4 = Reed switch [package=THT]
  S5 = Reed switch [package=THT]
  S6 = Reed switch [package=THT]
  S7 = Reed switch [package=THT]
  S8 = Reed switch [package=THT]
  S9 = Reed switch [package=THT]
  S10 = Reed switch [package=THT]
  S11 = Reed switch [package=THT]
  R16 = Resistor [tolerance=±5% resistance=10k package=THT]
  R17 = Resistor [tolerance=±5% resistance=10k package=THT]
  R18 = Resistor [tolerance=±5% resistance=10k package=THT]
  R19 = Resistor [tolerance=±5% resistance=10k package=THT]
  R20 = Resistor [tolerance=±5% resistance=10k package=THT]
  R21 = Resistor [tolerance=±5% resistance=10k package=THT]
  R22 = Resistor [tolerance=±5% resistance=10k package=THT]
  R23 = Resistor [tolerance=±5% resistance=10k package=THT]

nets:
  N1: Composant1.A0, R15.wiper
  N2: Composant1.A4, OLED_I2C1.SDA
  N3: Composant1.A5, OLED_I2C1.SCK
  N4: Composant1.SCL, LCD2004-I2C1.SCL
  N5: Composant1.SDA, LCD2004-I2C1.SDA
  GND: Composant1.GND, Composant2.GND, OLED_I2C1.GND, R11.Pin_1, R12.Pin_1, J3.pin1, LED3.cathode, R15.leg2, LCD2004-I2C1.GND, R16.Pin_1, R17.Pin_1, R18.Pin_1, R19.Pin_1, R20.Pin_1, R21.Pin_1, R22.Pin_1, R23.Pin_1
  N6: Composant1.D13_PWM, KeyLock.leg0, R12.Pin_0
  N7: Composant1.D12_PWM, S3.leg0, R11.Pin_0
  N8: Composant1.D11_PWM, Keypad4x1.Pin1
  N9: Composant1.D10_PWM, Keypad4x1.Pin2
  N10: Composant1.D9_PWM, Keypad4x1.Pin3
  N11: Composant1.D8_PWM, Keypad4x1.Pin4
  3V3: Composant1.3V3, Composant2.3.3V
  5V: Composant1.5V, Composant1.D45, Composant1.D46, Composant1.D47, Composant1.D48, OLED_I2C1.VDD, S3.leg1, KeyLock.leg1, R15.leg1, LCD2004-I2C1.VCC, S4.pin_1, S5.pin_1, S6.pin_1, S7.pin_1, S8.pin_1, S9.pin_1, S10.pin_1, S11.pin_1
  N12: Composant1.D2_PWM, R14.Pin_1
  N13: Composant1.D3_PWM, R13.Pin_1
  N14: Composant1.D4_PWM, Keypad4x1.Pin8
  N15: Composant1.D5_PWM, Keypad4x1.Pin7
  N16: Composant1.D6_PWM, Keypad4x1.Pin6
  N17: Composant1.D7_PWM, Keypad4x1.Pin5
  N18: Composant1.D24, S10.pin_2, R23.Pin_0
  N19: Composant1.D26, S8.pin_2, R22.Pin_0
  N20: Composant1.D28, S9.pin_2, R21.Pin_0
  N21: Composant1.D30, S11.pin_2, R20.Pin_0
  N22: Composant1.D32, S7.pin_2, R19.Pin_0
  N23: Composant1.D34, S6.pin_2, R18.Pin_0
  N24: Composant1.D36, S5.pin_2, R17.Pin_0
  N25: Composant1.D38, S4.pin_2, R16.Pin_0
  N26: Composant1.D43, Composant2.SDA
  N27: Composant1.D49, Composant2.RST
  N28: Composant1.D50, Composant2.MISO
  N29: Composant1.D51, Composant2.MOSI
  N30: Composant1.D52, Composant2.SCK

custom parts:
  RFID-RC522-v2: A simple China made RFID-RC522 Reader; do check the pin labels, as this is a MFRC522 based clone.
  Keypad Membran 4x4: Membrane Keypad 4x4 Matrix
  LCD2004-I2C: A standard character display with 4x20 characters. Comes in many colors with LCM2004 IIC attached.
